# Fritzing sketch circuit (saved by Fritzing 0.9.4)

parts:
  ZS-042_RTC1 = ZS-042 RTC Module
  Part2 = Arduino Nano (Rev3.0) (ICSP)
  8x8_LED_Modul_mit_MAX1 = 8x8 LED Modul mit MAX7219 [package=THT]
  S1 = Momentary Switch [package=ksa_sealed_tac_switch]

nets:
  GND: ZS-042_RTC1.GND, Part2.GND, 8x8_LED_Modul_mit_MAX1.GND_Eingang, S1.3
  VCC: ZS-042_RTC1.VCC, Part2.5V, 8x8_LED_Modul_mit_MAX1.VCC_Eingang
  N1: ZS-042_RTC1.SDA, Part2.A4
  N2: ZS-042_RTC1.SCL, Part2.A5
  N3: Part2.D3, 8x8_LED_Modul_mit_MAX1.CS_Eingang
  N4: Part2.D7, S1.1
  N5: Part2.D11/MOSI, 8x8_LED_Modul_mit_MAX1.DIN_Eingang
  N6: Part2.D13/SCK, 8x8_LED_Modul_mit_MAX1.CLK_Eingang
